// Logisim project cpu_works_no_bnez.circ as structural Verilog: 4 circuits, main circuit CPU
// R0
module CPU (
  output [9:0] out_1,
  output [9:0] out_2,
  output [9:0] out_3,
  output [9:0] out_4,
  output [9:0] out_5,
  output [4:0] Cout1,
  output [9:0] out_7,
  output [2:0] Cout1_2,
  output [9:0] out_9,
  output [2:0] Cout1_3,
  output [9:0] b_mux,
  output [2:0] Cout1_4,
  output [9:0] a_mux,
  output ignore,
  output [9:0] Cout1_5,
  output halt,
  output [4:0] Cout1_6,
  output [3:0] alu_opcode,
  output [9:0] out
);

  wire and_1_out, and_2_out, and_3_out, and_4_out, and_5_out, and_6_out, and_7_out, and_8_out, and_9_out,
       and_10_out, and_11_out, and_12_out, and_13_out, and_14_out, and_15_out, and_16_out, and_17_out,
       and_18_out, and_19_out, and_20_out, and_21_out, and_22_out, and_23_out, and_24_out, and_25_out,
       and_26_out, and_27_out, and_28_out, and_29_out, and_30_out, and_31_out, C11, CIN, CLK, clock_1_out,
       comparator_1_lt, comparator_2_lt, decoder_2_out7, decoder_2_out8, decoder_2_out9, decoder_2_out10,
       ENA, ENA1, ENA2, ENA3, ENA4, ENA5, ENA6, HALT_t, multiplexer_2_out, multiplexer_3_out,
       multiplexer_4_out, multiplexer_5_out, multiplexer_6_out, multiplexer_7_out, multiplexer_8_out,
       multiplexer_9_out, multiplexer_10_out, multiplexer_14_out, NOP, nor_1_out, not_1_out, not_3_out,
       not_4_out, not_5_out, not_6_out, not_7_out, not_8_out, not_9_out, not_10_out, not_11_out, not_12_out,
       not_13_out, not_14_out, not_15_out, not_16_out, not_17_out, not_18_out, not_19_out, not_20_out,
       not_21_out, not_22_out, or_1_out, or_2_out, or_3_out, or_4_out, or_5_out, or_6_out, or_7_out,
       or_8_out, or_9_out, or_10_out, or_11_out, or_12_out, or_13_out, or_14_out, or_15_out, or_16_out,
       or_17_out, or_18_out, or_20_out, or_22_out, t_ff_1_q, TClock, xor_1_out, xor_2_out, xor_3_out,
       xor_4_out, xor_5_out, xor_6_out, xor_7_out, xor_8_out, xor_9_out, xor_10_out, xor_11_out, xor_12_out,
       xor_13_out, xor_14_out, xor_15_out, xor_16_out, xor_17_out, xor_18_out, xor_19_out, xor_20_out;
  wire [1:0] counter_2_q, Upper_2_bits;
  wire [2:0] rom_1_data;
  wire [3:0] multiplexer_26_out;
  wire [4:0] counter_1_q, PC_address;
  wire [6:0] adder_1_out, adder_2_out, ASCII, LSB, MiddleBits;
  wire [7:0] multiplexer_1_out;

  TTY #(.rows(33), .cols(4)) tty_1 (.data(ASCII), .clk(TClock));  // open: we, clr
  // Probe on out_1
  // Probe on out_5
  Counter #(.width(5), .max('h1f), .ongoal("stay")) counter_1 (
    .Q(counter_1_q), .carry(halt), .clk(CLK));  // open: load, D, count, clr
  // Probe on out_2
  // Probe on out_7
  Multiplexer #(.select(3), .width(10)) multiplexer_1 (
    .in0(out_1), .in1(out_2), .in2(out_3), .in3(out_4), .in4(out_5), .in5(out_7), .in6(out_9),
    .out({Upper_2_bits, multiplexer_1_out}), .sel(rom_1_data));  // open: in7, en
  not not_1 (not_1_out, halt);
  Clock clock_1 (.out(clock_1_out));
  // Probe on out_3
  // Probe on out_9
  ROM #(.addrWidth(5), .dataWidth(3)) rom_1 (.addr(counter_1_q), .data(rom_1_data));  // open: sel
  and and_1 (and_1_out, not_1_out, clock_1_out);
  not not_2 (TClock, and_1_out);
  Multiplexer #(.enable("false")) multiplexer_2 (.in0(b_mux[2]), .in1(not_6_out), .out(multiplexer_2_out), .sel(CIN));
  // Probe on out_4
  T_Flip_Flop t_ff_1 (.clk(and_1_out), .T(1'b1), .Q(t_ff_1_q));  // open: Qn, preset, reset, en
  not not_3 (not_3_out, b_mux[8]);
  Multiplexer #(.enable("false")) multiplexer_3 (.in0(b_mux[8]), .in1(not_3_out), .out(multiplexer_3_out), .sel(CIN));
  not not_4 (not_4_out, b_mux[7]);
  Multiplexer #(.enable("false")) multiplexer_4 (.in0(b_mux[7]), .in1(not_4_out), .out(multiplexer_4_out), .sel(CIN));
  not not_5 (not_5_out, b_mux[3]);
  Multiplexer #(.enable("false")) multiplexer_5 (.in0(b_mux[3]), .in1(not_5_out), .out(multiplexer_5_out), .sel(CIN));
  not not_6 (not_6_out, b_mux[2]);
  Comparator #(.width(7)) comparator_1 (
    .a(7'b0111001), .b({3'b011, multiplexer_1_out[3:0]}), .lt(comparator_1_lt));  // open: gt, eq
  Comparator #(.width(7)) comparator_2 (
    .a(7'b0111001), .b({3'b011, multiplexer_1_out[7:4]}), .lt(comparator_2_lt));  // open: gt, eq
  Counter #(.width(2), .max('h3)) counter_2 (.Q(counter_2_q), .clk(TClock));  // open: load, D, count, carry, clr
  T_Flip_Flop t_ff_2 (.clk(t_ff_1_q), .T(1'b1), .Q(CLK));  // open: Qn, preset, reset, en
  Multiplexer #(.enable("false")) multiplexer_6 (.in0(b_mux[9]), .in1(not_15_out), .out(multiplexer_6_out), .sel(CIN));
  not not_7 (not_7_out, a_mux[8]);
  xor xor_1 (xor_1_out, a_mux[8], multiplexer_3_out);
  and and_2 (and_2_out, a_mux[8], multiplexer_3_out);
  not not_8 (not_8_out, a_mux[7]);
  not not_9 (not_9_out, b_mux[6]);
  Multiplexer #(.enable("false")) multiplexer_7 (.in0(b_mux[6]), .in1(not_9_out), .out(multiplexer_7_out), .sel(CIN));
  not not_10 (not_10_out, b_mux[5]);
  Multiplexer #(.enable("false")) multiplexer_8 (.in0(b_mux[5]), .in1(not_10_out), .out(multiplexer_8_out), .sel(CIN));
  not not_11 (not_11_out, a_mux[3]);
  not not_12 (not_12_out, a_mux[2]);
  not not_13 (not_13_out, b_mux[1]);
  Multiplexer #(.enable("false")) multiplexer_9 (.in0(b_mux[1]), .in1(not_13_out), .out(multiplexer_9_out), .sel(CIN));
  not not_14 (not_14_out, b_mux[0]);
  Multiplexer #(.enable("false")) multiplexer_10 (
    .in0(b_mux[0]), .in1(not_14_out), .out(multiplexer_10_out), .sel(CIN));
  Multiplexer #(.width(7), .disabled(0), .enable("false")) multiplexer_11 (
    .in0({3'b011, multiplexer_1_out[3:0]}), .in1(adder_1_out), .out(LSB), .sel(comparator_1_lt));
  Adder #(.width(7)) adder_1 (
    .a({3'b011, multiplexer_1_out[3:0]}), .b(7'b0000111), .out(adder_1_out));  // open: cin, cout
  Multiplexer #(.width(7), .disabled(0), .enable("false")) multiplexer_12 (
    .in0({3'b011, multiplexer_1_out[7:4]}), .in1(adder_2_out), .out(MiddleBits), .sel(comparator_2_lt));
  Adder #(.width(7)) adder_2 (
    .a({3'b011, multiplexer_1_out[7:4]}), .b(7'b0000111), .out(adder_2_out));  // open: cin, cout
  Multiplexer #(.select(2), .width(7)) multiplexer_13 (
    .in0({5'b01100, Upper_2_bits}), .in1(MiddleBits), .in2(LSB), .in3(7'b0100000), .out(ASCII),
    .sel(counter_2_q));  // open: en
  not not_15 (not_15_out, b_mux[9]);
  and and_3 (and_3_out, a_mux[8], b_mux[8]);
  or or_1 (or_1_out, a_mux[8], b_mux[8]);
  and and_4 (and_4_out, a_mux[7], b_mux[7]);
  or or_2 (or_2_out, a_mux[7], b_mux[7]);
  xor xor_2 (xor_2_out, a_mux[7], multiplexer_4_out);
  and and_5 (and_5_out, a_mux[6], b_mux[6]);
  or or_3 (or_3_out, a_mux[6], b_mux[6]);
  not not_16 (not_16_out, a_mux[6]);
  xor xor_3 (xor_3_out, a_mux[6], multiplexer_7_out);
  and and_6 (and_6_out, a_mux[6], multiplexer_7_out);
  and and_7 (and_7_out, a_mux[5], b_mux[5]);
  or or_4 (or_4_out, a_mux[5], b_mux[5]);
  not not_17 (not_17_out, a_mux[5]);
  xor xor_4 (xor_4_out, a_mux[5], multiplexer_8_out);
  and and_8 (and_8_out, a_mux[5], multiplexer_8_out);
  not not_18 (not_18_out, b_mux[4]);
  Multiplexer #(.enable("false")) multiplexer_14 (
    .in0(b_mux[4]), .in1(not_18_out), .out(multiplexer_14_out), .sel(CIN));
  and and_9 (and_9_out, a_mux[3], b_mux[3]);
  or or_5 (or_5_out, a_mux[3], b_mux[3]);
  xor xor_5 (xor_5_out, a_mux[3], multiplexer_5_out);
  and and_10 (and_10_out, a_mux[3], multiplexer_5_out);
  and and_11 (and_11_out, a_mux[2], b_mux[2]);
  or or_6 (or_6_out, a_mux[2], b_mux[2]);
  xor xor_6 (xor_6_out, a_mux[2], multiplexer_2_out);
  and and_12 (and_12_out, a_mux[1], b_mux[1]);
  or or_7 (or_7_out, a_mux[1], b_mux[1]);
  not not_19 (not_19_out, a_mux[1]);
  xor xor_7 (xor_7_out, a_mux[1], multiplexer_9_out);
  and and_13 (and_13_out, a_mux[1], multiplexer_9_out);
  and and_14 (and_14_out, a_mux[0], b_mux[0]);
  or or_8 (or_8_out, a_mux[0], b_mux[0]);
  not not_20 (not_20_out, a_mux[0]);
  xor xor_8 (xor_8_out, a_mux[0], multiplexer_10_out);
  and and_15 (and_15_out, a_mux[0], multiplexer_10_out);
  and and_16 (and_16_out, a_mux[9], b_mux[9]);
  or or_9 (or_9_out, a_mux[9], b_mux[9]);
  not not_21 (not_21_out, a_mux[9]);
  xor xor_9 (xor_9_out, a_mux[9], multiplexer_6_out);
  and and_17 (and_17_out, a_mux[9], multiplexer_6_out);
  xor xor_10 (xor_10_out, xor_2_out, or_16_out);
  xor xor_11 (xor_11_out, xor_4_out, or_20_out);
  and and_18 (and_18_out, xor_4_out, or_20_out);
  and and_19 (and_19_out, a_mux[4], b_mux[4]);
  or or_10 (or_10_out, a_mux[4], b_mux[4]);
  not not_22 (not_22_out, a_mux[4]);
  xor xor_12 (xor_12_out, a_mux[4], multiplexer_14_out);
  and and_20 (and_20_out, a_mux[4], multiplexer_14_out);
  xor xor_13 (xor_13_out, xor_8_out, CIN);
  and and_21 (and_21_out, xor_8_out, CIN);
  nor nor_1 (nor_1_out, NOP, HALT_t);
  T_Flip_Flop t_ff_3 (.clk(CLK), .T(1'b1), .Q(ignore));  // open: Qn, preset, reset, en
  xor xor_14 (xor_14_out, xor_1_out, or_12_out);
  and and_22 (and_22_out, xor_1_out, or_12_out);
  and and_23 (and_23_out, or_16_out, xor_2_out);
  and and_24 (and_24_out, a_mux[7], multiplexer_4_out);
  xor xor_15 (xor_15_out, xor_3_out, or_13_out);
  and and_25 (and_25_out, xor_3_out, or_13_out);
  xor xor_16 (xor_16_out, xor_5_out, or_17_out);
  and and_26 (and_26_out, xor_5_out, or_17_out);
  xor xor_17 (xor_17_out, xor_6_out, or_18_out);
  and and_27 (and_27_out, or_18_out, xor_6_out);
  and and_28 (and_28_out, a_mux[2], multiplexer_2_out);
  xor xor_18 (xor_18_out, xor_7_out, or_15_out);
  and and_29 (and_29_out, xor_7_out, or_15_out);
  D_Flip_Flop d_ff_1 (.clk(CLK), .D(out[9]), .Q(out_1[9]), .en(ENA));  // open: Qn, preset, reset
  D_Flip_Flop d_ff_2 (.clk(CLK), .D(out[8]), .Q(out_1[8]), .en(ENA));  // open: Qn, preset, reset
  D_Flip_Flop d_ff_3 (.clk(CLK), .D(out[7]), .Q(out_1[7]), .en(ENA));  // open: Qn, preset, reset
  D_Flip_Flop d_ff_4 (.clk(CLK), .D(out[6]), .Q(out_1[6]), .en(ENA));  // open: Qn, preset, reset
  D_Flip_Flop d_ff_5 (.clk(CLK), .D(out[5]), .Q(out_1[5]), .en(ENA));  // open: Qn, preset, reset
  D_Flip_Flop d_ff_6 (.clk(CLK), .D(out[4]), .Q(out_1[4]), .en(ENA));  // open: Qn, preset, reset
  D_Flip_Flop d_ff_7 (.clk(CLK), .D(out[3]), .Q(out_1[3]), .en(ENA));  // open: Qn, preset, reset
  D_Flip_Flop d_ff_8 (.clk(CLK), .D(out[2]), .Q(out_1[2]), .en(ENA));  // open: Qn, preset, reset
  D_Flip_Flop d_ff_9 (.clk(CLK), .D(out[1]), .Q(out_1[1]), .en(ENA));  // open: Qn, preset, reset
  D_Flip_Flop d_ff_10 (.clk(CLK), .D(out[0]), .Q(out_1[0]), .en(ENA));  // open: Qn, preset, reset
  xor xor_19 (xor_19_out, xor_9_out, or_11_out);
  and and_30 (and_30_out, xor_9_out, or_11_out);
  or or_11 (or_11_out, and_22_out, and_2_out);
  or or_12 (or_12_out, and_23_out, and_24_out);
  Multiplexer #(.select(4), .enable("false")) multiplexer_15 (
    .in0(and_7_out), .in1(or_4_out), .in2(not_17_out), .in3(xor_11_out), .in4(a_mux[5]), .in5(a_mux[4]),
    .in6(a_mux[6]), .in7(xor_11_out), .in8(xor_11_out), .in9(xor_11_out), .in10(b_mux[5]), .out(out[5]),
    .sel(alu_opcode));  // open: in11, in12, in13, in14, in15
  or or_13 (or_13_out, and_18_out, and_8_out);
  xor xor_20 (xor_20_out, xor_12_out, or_14_out);
  and and_31 (and_31_out, xor_12_out, or_14_out);
  or or_14 (or_14_out, and_26_out, and_10_out);
  Multiplexer #(.select(4), .enable("false")) multiplexer_16 (
    .in0(and_14_out), .in1(or_8_out), .in2(not_20_out), .in3(xor_13_out), .in4(a_mux[0]), .in5(1'b0),
    .in6(a_mux[1]), .in7(xor_13_out), .in8(xor_13_out), .in9(xor_13_out), .in10(b_mux[0]), .out(out[0]),
    .sel(alu_opcode));  // open: in11, in12, in13, in14, in15
  or or_15 (or_15_out, and_21_out, and_15_out);
  D_Flip_Flop d_ff_11 (.clk(CLK), .D(out[9]), .Q(out_2[9]), .en(ENA1));  // open: Qn, preset, reset
  D_Flip_Flop d_ff_12 (.clk(CLK), .D(out[8]), .Q(out_2[8]), .en(ENA1));  // open: Qn, preset, reset
  D_Flip_Flop d_ff_13 (.clk(CLK), .D(out[7]), .Q(out_2[7]), .en(ENA1));  // open: Qn, preset, reset
  D_Flip_Flop d_ff_14 (.clk(CLK), .D(out[6]), .Q(out_2[6]), .en(ENA1));  // open: Qn, preset, reset
  D_Flip_Flop d_ff_15 (.clk(CLK), .D(out[5]), .Q(out_2[5]), .en(ENA1));  // open: Qn, preset, reset
  D_Flip_Flop d_ff_16 (.clk(CLK), .D(out[4]), .Q(out_2[4]), .en(ENA1));  // open: Qn, preset, reset
  D_Flip_Flop d_ff_17 (.clk(CLK), .D(out[3]), .Q(out_2[3]), .en(ENA1));  // open: Qn, preset, reset
  D_Flip_Flop d_ff_18 (.clk(CLK), .D(out[2]), .Q(out_2[2]), .en(ENA1));  // open: Qn, preset, reset
  D_Flip_Flop d_ff_19 (.clk(CLK), .D(out[1]), .Q(out_2[1]), .en(ENA1));  // open: Qn, preset, reset
  D_Flip_Flop d_ff_20 (.clk(CLK), .D(out[0]), .Q(out_2[0]), .en(ENA1));  // open: Qn, preset, reset
  Multiplexer #(.select(4), .enable("false")) multiplexer_17 (
    .in0(and_4_out), .in1(or_2_out), .in2(not_8_out), .in3(xor_10_out), .in4(a_mux[7]), .in5(a_mux[6]),
    .in6(a_mux[8]), .in7(xor_10_out), .in8(xor_10_out), .in9(xor_10_out), .in10(b_mux[7]), .out(out[7]),
    .sel(alu_opcode));  // open: in11, in12, in13, in14, in15
  or or_16 (or_16_out, and_25_out, and_6_out);
  or or_17 (or_17_out, and_27_out, and_28_out);
  or or_18 (or_18_out, and_29_out, and_13_out);
  Decoder #(.select(3)) decoder_1 (
    .out0(ENA), .out1(ENA1), .out2(ENA2), .out3(ENA3), .out4(ENA4), .out5(ENA5), .out6(ENA6), .sel(Cout1_2),
    .en(nor_1_out));  // open: out7
  D_Flip_Flop d_ff_21 (.clk(CLK), .D(out[9]), .Q(out_3[9]), .en(ENA2));  // open: Qn, preset, reset
  D_Flip_Flop d_ff_22 (.clk(CLK), .D(out[8]), .Q(out_3[8]), .en(ENA2));  // open: Qn, preset, reset
  D_Flip_Flop d_ff_23 (.clk(CLK), .D(out[7]), .Q(out_3[7]), .en(ENA2));  // open: Qn, preset, reset
  D_Flip_Flop d_ff_24 (.clk(CLK), .D(out[6]), .Q(out_3[6]), .en(ENA2));  // open: Qn, preset, reset
  D_Flip_Flop d_ff_25 (.clk(CLK), .D(out[5]), .Q(out_3[5]), .en(ENA2));  // open: Qn, preset, reset
  D_Flip_Flop d_ff_26 (.clk(CLK), .D(out[4]), .Q(out_3[4]), .en(ENA2));  // open: Qn, preset, reset
  D_Flip_Flop d_ff_27 (.clk(CLK), .D(out[3]), .Q(out_3[3]), .en(ENA2));  // open: Qn, preset, reset
  D_Flip_Flop d_ff_28 (.clk(CLK), .D(out[2]), .Q(out_3[2]), .en(ENA2));  // open: Qn, preset, reset
  D_Flip_Flop d_ff_29 (.clk(CLK), .D(out[1]), .Q(out_3[1]), .en(ENA2));  // open: Qn, preset, reset
  D_Flip_Flop d_ff_30 (.clk(CLK), .D(out[0]), .Q(out_3[0]), .en(ENA2));  // open: Qn, preset, reset
  or or_19 (C11, and_30_out, and_17_out);
  Multiplexer #(.select(4), .enable("false")) multiplexer_18 (
    .in0(and_3_out), .in1(or_1_out), .in2(not_7_out), .in3(xor_14_out), .in4(a_mux[8]), .in5(a_mux[7]),
    .in6(a_mux[9]), .in7(xor_14_out), .in8(xor_14_out), .in9(xor_14_out), .in10(b_mux[8]), .out(out[8]),
    .sel(alu_opcode));  // open: in11, in12, in13, in14, in15
  Multiplexer #(.select(4), .enable("false")) multiplexer_19 (
    .in0(and_5_out), .in1(or_3_out), .in2(not_16_out), .in3(xor_15_out), .in4(a_mux[6]), .in5(a_mux[5]),
    .in6(a_mux[7]), .in7(xor_15_out), .in8(xor_15_out), .in9(xor_15_out), .in10(b_mux[6]), .out(out[6]),
    .sel(alu_opcode));  // open: in11, in12, in13, in14, in15
  or or_20 (or_20_out, and_31_out, and_20_out);
  Multiplexer #(.select(4), .enable("false")) multiplexer_20 (
    .in0(and_11_out), .in1(or_6_out), .in2(not_12_out), .in3(xor_17_out), .in4(a_mux[2]), .in5(a_mux[1]),
    .in6(a_mux[3]), .in7(xor_17_out), .in8(xor_17_out), .in9(xor_17_out), .in10(b_mux[2]), .out(out[2]),
    .sel(alu_opcode));  // open: in11, in12, in13, in14, in15
  Multiplexer #(.select(4), .enable("false")) multiplexer_21 (
    .in0(and_12_out), .in1(or_7_out), .in2(not_19_out), .in3(xor_18_out), .in4(a_mux[1]), .in5(a_mux[0]),
    .in6(a_mux[2]), .in7(xor_18_out), .in8(xor_18_out), .in9(xor_18_out), .in10(b_mux[1]), .out(out[1]),
    .sel(alu_opcode));  // open: in11, in12, in13, in14, in15
  Multiplexer #(.select(4), .enable("false")) multiplexer_22 (
    .in0(and_9_out), .in1(or_5_out), .in2(not_11_out), .in3(xor_16_out), .in4(a_mux[3]), .in5(a_mux[2]),
    .in6(a_mux[4]), .in7(xor_16_out), .in8(xor_16_out), .in9(xor_16_out), .in10(b_mux[3]), .out(out[3]),
    .sel(alu_opcode));  // open: in11, in12, in13, in14, in15
  PC PC (.CLK(CLK), .Address(PC_address), .HLT(HALT_t));
  Multiplexer #(.select(4), .enable("false")) multiplexer_23 (
    .in0(and_16_out), .in1(or_9_out), .in2(not_21_out), .in3(xor_19_out), .in4(a_mux[9]), .in5(a_mux[8]),
    .in6(1'b0), .in7(xor_19_out), .in8(xor_19_out), .in9(xor_19_out), .in10(b_mux[9]), .out(out[9]),
    .sel(alu_opcode));  // open: in11, in12, in13, in14, in15
  Multiplexer #(.select(4), .enable("false")) multiplexer_24 (
    .in0(and_19_out), .in1(or_10_out), .in2(not_22_out), .in3(xor_20_out), .in4(a_mux[4]), .in5(a_mux[3]),
    .in6(a_mux[5]), .in7(xor_20_out), .in8(xor_20_out), .in9(xor_20_out), .in10(b_mux[4]), .out(out[4]),
    .sel(alu_opcode));  // open: in11, in12, in13, in14, in15
  RAM #(.addrWidth(5), .dataWidth(24), .bus("separate")) ram_1 (
    .addr(PC_address), .data({Cout1[4], alu_opcode, Cout1_2, Cout1_3, Cout1_4, Cout1_5}));  // open: din, str, sel, clk, ld, clr
  D_Flip_Flop d_ff_31 (.clk(CLK), .D(out[9]), .Q(out_4[9]), .en(ENA3));  // open: Qn, preset, reset
  D_Flip_Flop d_ff_32 (.clk(CLK), .D(out[8]), .Q(out_4[8]), .en(ENA3));  // open: Qn, preset, reset
  D_Flip_Flop d_ff_33 (.clk(CLK), .D(out[7]), .Q(out_4[7]), .en(ENA3));  // open: Qn, preset, reset
  D_Flip_Flop d_ff_34 (.clk(CLK), .D(out[6]), .Q(out_4[6]), .en(ENA3));  // open: Qn, preset, reset
  D_Flip_Flop d_ff_35 (.clk(CLK), .D(out[5]), .Q(out_4[5]), .en(ENA3));  // open: Qn, preset, reset
  D_Flip_Flop d_ff_36 (.clk(CLK), .D(out[4]), .Q(out_4[4]), .en(ENA3));  // open: Qn, preset, reset
  D_Flip_Flop d_ff_37 (.clk(CLK), .D(out[3]), .Q(out_4[3]), .en(ENA3));  // open: Qn, preset, reset
  D_Flip_Flop d_ff_38 (.clk(CLK), .D(out[2]), .Q(out_4[2]), .en(ENA3));  // open: Qn, preset, reset
  D_Flip_Flop d_ff_39 (.clk(CLK), .D(out[1]), .Q(out_4[1]), .en(ENA3));  // open: Qn, preset, reset
  D_Flip_Flop d_ff_40 (.clk(CLK), .D(out[0]), .Q(out_4[0]), .en(ENA3));  // open: Qn, preset, reset
  D_Flip_Flop d_ff_41 (.clk(CLK), .D(out[9]), .Q(out_5[9]), .en(ENA4));  // open: Qn, preset, reset
  D_Flip_Flop d_ff_42 (.clk(CLK), .D(out[8]), .Q(out_5[8]), .en(ENA4));  // open: Qn, preset, reset
  D_Flip_Flop d_ff_43 (.clk(CLK), .D(out[7]), .Q(out_5[7]), .en(ENA4));  // open: Qn, preset, reset
  D_Flip_Flop d_ff_44 (.clk(CLK), .D(out[6]), .Q(out_5[6]), .en(ENA4));  // open: Qn, preset, reset
  D_Flip_Flop d_ff_45 (.clk(CLK), .D(out[5]), .Q(out_5[5]), .en(ENA4));  // open: Qn, preset, reset
  D_Flip_Flop d_ff_46 (.clk(CLK), .D(out[4]), .Q(out_5[4]), .en(ENA4));  // open: Qn, preset, reset
  D_Flip_Flop d_ff_47 (.clk(CLK), .D(out[3]), .Q(out_5[3]), .en(ENA4));  // open: Qn, preset, reset
  D_Flip_Flop d_ff_48 (.clk(CLK), .D(out[2]), .Q(out_5[2]), .en(ENA4));  // open: Qn, preset, reset
  D_Flip_Flop d_ff_49 (.clk(CLK), .D(out[1]), .Q(out_5[1]), .en(ENA4));  // open: Qn, preset, reset
  D_Flip_Flop d_ff_50 (.clk(CLK), .D(out[0]), .Q(out_5[0]), .en(ENA4));  // open: Qn, preset, reset
  Multiplexer #(.select(3), .width(10), .enable("false")) multiplexer_25 (
    .in0(out_1), .in1(out_2), .in2(out_3), .in3(out_4), .in4(out_5), .in5(out_7), .in6(out_9), .out(a_mux),
    .sel(Cout1_3));  // open: in7
  D_Flip_Flop d_ff_51 (.clk(CLK), .D(out[9]), .Q(out_7[9]), .en(ENA5));  // open: Qn, preset, reset
  D_Flip_Flop d_ff_52 (.clk(CLK), .D(out[8]), .Q(out_7[8]), .en(ENA5));  // open: Qn, preset, reset
  D_Flip_Flop d_ff_53 (.clk(CLK), .D(out[7]), .Q(out_7[7]), .en(ENA5));  // open: Qn, preset, reset
  D_Flip_Flop d_ff_54 (.clk(CLK), .D(out[6]), .Q(out_7[6]), .en(ENA5));  // open: Qn, preset, reset
  D_Flip_Flop d_ff_55 (.clk(CLK), .D(out[5]), .Q(out_7[5]), .en(ENA5));  // open: Qn, preset, reset
  D_Flip_Flop d_ff_56 (.clk(CLK), .D(out[4]), .Q(out_7[4]), .en(ENA5));  // open: Qn, preset, reset
  D_Flip_Flop d_ff_57 (.clk(CLK), .D(out[3]), .Q(out_7[3]), .en(ENA5));  // open: Qn, preset, reset
  D_Flip_Flop d_ff_58 (.clk(CLK), .D(out[2]), .Q(out_7[2]), .en(ENA5));  // open: Qn, preset, reset
  D_Flip_Flop d_ff_59 (.clk(CLK), .D(out[1]), .Q(out_7[1]), .en(ENA5));  // open: Qn, preset, reset
  D_Flip_Flop d_ff_60 (.clk(CLK), .D(out[0]), .Q(out_7[0]), .en(ENA5));  // open: Qn, preset, reset
  Decoder #(.select(5), .enable("false")) decoder_2 (
    .out7(decoder_2_out7), .out8(decoder_2_out8), .out9(decoder_2_out9), .out10(decoder_2_out10),
    .out12(NOP), .out31(HALT_t), .sel({Cout1[4], alu_opcode}));  // open: out0, out1, out2, out3, out4, out5, out6, out11, out13, out14, out15, out16, out17, out18, out19, out20, out21, out22, out23, out24, out25, out26, out27, out28, out29, out30
  or or_21 (CIN, decoder_2_out7, decoder_2_out9);
  or or_22 (or_22_out, decoder_2_out8, decoder_2_out9, decoder_2_out10);
  Multiplexer #(.width(4), .enable("false")) multiplexer_26 (
    .in0({1'b0, Cout1_4}), .in1(4'b1000), .out(multiplexer_26_out), .sel(or_22_out));
  Multiplexer #(.select(4), .width(10), .enable("false")) multiplexer_27 (
    .in0(out_1), .in1(out_2), .in2(out_3), .in3(out_4), .in4(out_5), .in5(out_7), .in6(out_9),
    .in7({10{1'b0}}), .in8(Cout1_5), .out(b_mux), .sel(multiplexer_26_out));  // open: in9, in10, in11, in12, in13, in14, in15
  D_Flip_Flop d_ff_61 (.clk(CLK), .D(out[9]), .Q(out_9[9]), .en(ENA6));  // open: Qn, preset, reset
  D_Flip_Flop d_ff_62 (.clk(CLK), .D(out[8]), .Q(out_9[8]), .en(ENA6));  // open: Qn, preset, reset
  D_Flip_Flop d_ff_63 (.clk(CLK), .D(out[7]), .Q(out_9[7]), .en(ENA6));  // open: Qn, preset, reset
  D_Flip_Flop d_ff_64 (.clk(CLK), .D(out[6]), .Q(out_9[6]), .en(ENA6));  // open: Qn, preset, reset
  D_Flip_Flop d_ff_65 (.clk(CLK), .D(out[5]), .Q(out_9[5]), .en(ENA6));  // open: Qn, preset, reset
  D_Flip_Flop d_ff_66 (.clk(CLK), .D(out[4]), .Q(out_9[4]), .en(ENA6));  // open: Qn, preset, reset
  D_Flip_Flop d_ff_67 (.clk(CLK), .D(out[3]), .Q(out_9[3]), .en(ENA6));  // open: Qn, preset, reset
  D_Flip_Flop d_ff_68 (.clk(CLK), .D(out[2]), .Q(out_9[2]), .en(ENA6));  // open: Qn, preset, reset
  D_Flip_Flop d_ff_69 (.clk(CLK), .D(out[1]), .Q(out_9[1]), .en(ENA6));  // open: Qn, preset, reset
  D_Flip_Flop d_ff_70 (.clk(CLK), .D(out[0]), .Q(out_9[0]), .en(ENA6));  // open: Qn, preset, reset

  assign Cout1[3:0] = alu_opcode;
  assign Cout1_6 = {Cout1[4], alu_opcode};

  // Other names for the same wires on the sheet: MUX_B[2:0] = Cout1_4; A0 = a_mux[0]; A1 = a_mux[1]; A2 = a_mux[2];
  //   A3 = a_mux[3]; A4 = a_mux[4]; A5 = a_mux[5]; A6 = a_mux[6]; A7 = a_mux[7]; A8 = a_mux[8]; A9 = a_mux[9];
  //   opcode[4:0] = {Cout1[4], alu_opcode}; S0 = alu_opcode[0]; S1 = alu_opcode[1]; S2 = alu_opcode[2];
  //   S3 = alu_opcode[3]; B0 = b_mux[0]; B1 = b_mux[1]; B2 = b_mux[2]; B3 = b_mux[3]; B4 = b_mux[4]; B5 = b_mux[5];
  //   B6 = b_mux[6]; B7 = b_mux[7]; B8 = b_mux[8]; B9 = b_mux[9]; D = CIN; Data[9:0] = Cout1_5; MUX_A[2:0] = Cout1_3;
  //   no_need = Cout1[4]; C0 = out[0]; C1 = out[1]; C2 = out[2]; C3 = out[3]; C4 = out[4]; C6 = out[5]; C7 = out[6];
  //   C8 = out[7]; C9 = out[8]; C10 = out[9]; R0[9:0] = out_1; R1[9:0] = out_2; R2[9:0] = out_3; R3[9:0] = out_4;
  //   R4[9:0] = out_5; R5[9:0] = out_7; R6[9:0] = out_9; register[2:0] = Cout1_2

  // Notes on the sheet:
  //   DO NOT PUT ANY PINS ON THE main circuit.  (You should not need any anyway.)
  //   0F5
  //   0F5
  //   25A
  //   050
  //   2FF
  //   30A
  //   34F
  //   0F5
  //   1EA
  //   07A
  //   29B
  //   165
  //   10F
  //   0F5
  //   0AA
  //   0AA
  //   05A
  //   00A
  //   0FA
  //   104
  //   0B4
  //   165
  //   165
  //   001
  //   001
  //   000
  //   000
  //   000
  //   000
  //   000
  //   ???
  //   There is no Reset.  Just Ctrl-r, then load test.txt into your RAM, and then Ctrl-k
  //   You must  use the CLK tunnel for the source of your clock.  R0-R6 are the other tunnels you need to connect
  //   contents of rom_1 (hex, n*v repeats v):
  //   0 0 0 1 2 3 4 5 6 2 3 4 5 6 0 0 0 1 3 4 6 3 5 5 8*6
  //   ALU with subtraction 
  //   If NOP or HALT is true, decoder outputs 0 so no registers used
  //   Registers
  //   Enable which register to store data
  //   counter  for PC, add 1 each cycle, indicates which address to read instructions from
  //   0000 AND
  //   0001 OR
  //   0010 NOT
  //   0011 ADD
  //   0100 MOV
  //   0101 SLL
  //   0110 SRL
  //   0111 SUB
  //   1000  ADDI
  //   1001 SUBI
  //   MOVI 1010
  //   RAM
  //   Control Unit
  //   Retriving instructions from RAM, breaking bits into sections
  //   Source Register A, choose which register value to use
  //   Determines which opcode is in immedieate mode
  //   If in immedieate mode, MUX chooses input from 1, data register is 0111
  //   opcode requires subtraction
  //   Destination Register B
endmodule

module PC (
  input  CLK,
  input  HLT,
  output [4:0] Address
);

  wire and_1_out, and_2_out, and_3_out, not_1_out, not_2_out;

  not not_1 (not_1_out, CLK);
  not not_2 (not_2_out, HLT);
  T_Flip_Flop t_ff_1 (.clk(not_1_out), .T(1'b1), .Q(Address[0]), .en(not_2_out));  // open: Qn, preset, reset
  T_Flip_Flop t_ff_2 (.clk(not_1_out), .T(Address[0]), .Q(Address[1]), .en(not_2_out));  // open: Qn, preset, reset
  and and_1 (and_1_out, Address[1], Address[0]);
  T_Flip_Flop t_ff_3 (.clk(not_1_out), .T(and_1_out), .Q(Address[2]), .en(not_2_out));  // open: Qn, preset, reset
  and and_2 (and_2_out, Address[2], and_1_out);
  T_Flip_Flop t_ff_4 (.clk(not_1_out), .T(and_2_out), .Q(Address[3]), .en(not_2_out));  // open: Qn, preset, reset
  and and_3 (and_3_out, Address[3], and_2_out);
  T_Flip_Flop t_ff_5 (.clk(not_1_out), .T(and_3_out), .Q(Address[4]), .en(not_2_out));  // open: Qn, preset, reset

  // Other names for the same wires on the sheet: P0 = Address[0]; P1 = Address[1]; P2 = Address[2]; P3 = Address[3];
  //   P4 = Address[4]
endmodule

module register (
  input  Enable,
  output [9:0] INPUT,
  output [9:0] RVALUE
);

  wire CLK;

  D_Flip_Flop d_ff_1 (.clk(CLK), .D(INPUT[9]), .Q(RVALUE[9]), .en(Enable));  // open: Qn, preset, reset
  D_Flip_Flop d_ff_2 (.clk(CLK), .D(INPUT[8]), .Q(RVALUE[8]), .en(Enable));  // open: Qn, preset, reset
  D_Flip_Flop d_ff_3 (.clk(CLK), .D(INPUT[7]), .Q(RVALUE[7]), .en(Enable));  // open: Qn, preset, reset
  D_Flip_Flop d_ff_4 (.clk(CLK), .D(INPUT[6]), .Q(RVALUE[6]), .en(Enable));  // open: Qn, preset, reset
  D_Flip_Flop d_ff_5 (.clk(CLK), .D(INPUT[5]), .Q(RVALUE[5]), .en(Enable));  // open: Qn, preset, reset
  D_Flip_Flop d_ff_6 (.clk(CLK), .D(INPUT[4]), .Q(RVALUE[4]), .en(Enable));  // open: Qn, preset, reset
  D_Flip_Flop d_ff_7 (.clk(CLK), .D(INPUT[3]), .Q(RVALUE[3]), .en(Enable));  // open: Qn, preset, reset
  D_Flip_Flop d_ff_8 (.clk(CLK), .D(INPUT[2]), .Q(RVALUE[2]), .en(Enable));  // open: Qn, preset, reset
  D_Flip_Flop d_ff_9 (.clk(CLK), .D(INPUT[1]), .Q(RVALUE[1]), .en(Enable));  // open: Qn, preset, reset
  D_Flip_Flop d_ff_10 (.clk(CLK), .D(INPUT[0]), .Q(RVALUE[0]), .en(Enable));  // open: Qn, preset, reset
endmodule

module ALU (
  input  SUB_MUX,
  input  CARRY,
  output [4:0] opcode,
  output [9:0] A_INPUT,
  output [9:0] OUT,
  output [9:0] B_INPUT
);

  wire undriven, undriven_2, undriven_4, undriven_5, undriven_6, undriven_7, undriven_8, undriven_9,
       undriven_10;
  wire [3:0] undriven_3;

  Multiplexer #(.select(4), .enable("false")) multiplexer_1 (.out(OUT[9]));  // open: in0, in1, in2, in3, in4, in5, in6, in7, in8, in9, in10, in11, in12, in13, in14, in15, sel
  Multiplexer #(.select(4), .enable("false")) multiplexer_2 (
    .in0(undriven_4), .in1(undriven), .in2(undriven_2), .in3(undriven_6), .in4(undriven_5), .in7(undriven_7),
    .in8(undriven_8), .in9(undriven_9), .in10(undriven_10), .out(OUT[4]), .sel(undriven_3));  // open: in5, in6, in11, in12, in13, in14, in15

  // Other names for the same wires on the sheet: A0 = A_INPUT[0]; A1 = A_INPUT[1]; A2 = A_INPUT[2]; A3 = A_INPUT[3];
  //   A4 = A_INPUT[4]; A5 = A_INPUT[5]; A6 = A_INPUT[6]; A7 = A_INPUT[7]; A8 = A_INPUT[8]; A9 = A_INPUT[9];
  //   B0 = B_INPUT[0]; B1 = B_INPUT[1]; B2 = B_INPUT[2]; B3 = B_INPUT[3]; B4 = B_INPUT[4]; B5 = B_INPUT[5];
  //   B6 = B_INPUT[6]; B7 = B_INPUT[7]; B8 = B_INPUT[8]; B9 = B_INPUT[9]; CIN = CARRY; D = SUB_MUX; S0 = opcode[0];
  //   S1 = opcode[1]; S2 = opcode[2]; S3 = opcode[3]; C0 = OUT[0]; C1 = OUT[1]; C2 = OUT[2]; C3 = OUT[3]; C4 = OUT[4];
  //   C6 = OUT[5]; C7 = OUT[6]; C8 = OUT[7]; C9 = OUT[8]; C10 = OUT[9]
endmodule
